// Logisim project Circuito.circ as structural Verilog: 16 circuits, main circuit ULA
module Main (
);

  wire clock_1_out, not_1_out, not_2_out, OVERFLOW_q, RST_out, uc_1_clk_ac, uc_1_clk_ir, uc_1_clk_pc,
       uc_1_clk_ram, uc_1_e, uc_1_load, uc_1_r_w___0, uc_1_reset_pc, ula_1_overflow, ula_1_zero, ZERO_q;
  wire [2:0] uc_1_opcode;
  wire [3:0] ac_1_out_3, counter_1_q, mux_1_out_4, ram_1_data, uc_1_dados, uc_1_operando, ula_1_s;
  wire [7:0] ir_1_q, rom_1_data;

  not not_1 (not_1_out, uc_1_load);
  Counter #(.width(4), .max('hf), .trigger("falling")) counter_1 (
    .load(uc_1_load), .D(uc_1_dados), .count(not_1_out), .Q(counter_1_q), .clk(uc_1_clk_pc),
    .clr(uc_1_reset_pc));  // open: carry
  UC uc_1 (
    .\iNSTRUÇÃO (ir_1_q), .OPERANDO(uc_1_operando), .E(uc_1_e), .OPCODE(uc_1_opcode), .Clock(clock_1_out),
    .Reset(RST_out), .CLK_IR(uc_1_clk_ir), .CLK_PC(uc_1_clk_pc), .CLK_AC(uc_1_clk_ac),
    .CLK_RAM(uc_1_clk_ram), .R_W___0(uc_1_r_w___0), .Reset_pc(uc_1_reset_pc), .zero(ZERO_q),
    .Overflow(OVERFLOW_q), .LOAD(uc_1_load), .Dados(uc_1_dados));
  Clock clock_1 (.out(clock_1_out));
  // Probe on rom_1_data
  ROM #(.addrWidth(4)) rom_1 (.addr(counter_1_q), .data(rom_1_data));  // open: sel
  Button RST (.out(RST_out));
  IR ir_1 (.Clock(uc_1_clk_ir), .Q(ir_1_q), .E(rom_1_data));
  // Probe on ir_1_q
  // Probe on ac_1_out_3
  // Probe on uc_1_opcode
  MUX mux_1 (.C(uc_1_e), .A(uc_1_operando), .B(ram_1_data), .out_4(mux_1_out_4));
  ULA ula_1 (
    .A(ac_1_out_3), .B(mux_1_out_4), .S(ula_1_s), .in_4(uc_1_opcode), .D(uc_1_e), .Overflow(ula_1_overflow),
    .Zero(ula_1_zero));
  AC ac_1 (.Clock(uc_1_clk_ac), .out_3(ac_1_out_3), .E(ula_1_s));
  // Probe on mux_1_out_4
  // Probe on ula_1_s
  RAM #(.addrWidth(4), .dataWidth(4)) ram_1 (
    .addr(uc_1_operando), .data(ram_1_data), .clk(uc_1_clk_ram), .ld(uc_1_r_w___0));  // open: sel, clr
  D_Flip_Flop OVERFLOW (.clk(uc_1_clk_ac), .D(ula_1_overflow), .Q(OVERFLOW_q));  // open: Qn, preset, en, reset
  D_Flip_Flop ZERO (.clk(uc_1_clk_ac), .D(ula_1_zero), .Q(ZERO_q));  // open: Qn, preset, en, reset
  not not_2 (not_2_out, uc_1_r_w___0);
  Buffer buffer_1 (.C(not_2_out), .S(ram_1_data), .B(ac_1_out_3));

  // Notes on the sheet:
  //   0
  //   1
  //   2
  //   3
  //   4
  //   5
  //   6
  //   7
  //   8
  //   9
  //   A
  //   B
  //   C
  //   D
  //   E
  //   F
  //   MOV
  //   000 0
  //   000 1
  //   MOV
  //   ADD
  //   001 0
  //   001 1
  //   ADD
  //   010 0
  //   SUB
  //   SUB
  //   010 1
  //   011 0
  //   OR
  //   OR
  //   011 1
  //   NOT
  //   100 0
  //   100 1
  //   NOT
  //   SHF
  //   101 0
  //   101 1
  //   SHF
  //   JPZ
  //   110 0
  //   110 1 
  //   JPO
  //   111 0
  //   GO
  //   STR
  //   111 1
  //   Instruction Set
  //   AC <= X 
  //   AC <= M(X) 
  //   AC <= AC+X 
  //   AC <= AC+M(X)
  //   AC <= AC-X
  //   AC <= AC-M(X)
  //   AC <= AC OR X
  //   AC <= AR OR M(X)
  //   AC <= AR NOT X
  //   AC <= AR NOT M(X)
  //   AC <=  AC << Q
  //   AC <= AC >> Q
  //   PC <= X SE FLAG Z
  //   PC <= X SE FLAG O
  //   PC <= X
  //   M(X) <= AC
  //   Memória de programa
  //   contents of rom_1 (hex, n*v repeats v):
  //   1 f0 1 f1 10 31 d0 f2 11 f0 12 f1 e4
  //   Memória de Dados
endmodule

module ULA (
  input  D,
  input  [3:0] B,
  input  [3:0] A,
  input  [2:0] in_4,
  output Overflow,
  output [3:0] S,
  output Zero
);

  wire add_4_1_overflow, and_1_out, and_2_out, dec3x8_1_a, dec3x8_1_b, dec3x8_1_c, dec3x8_1_d, dec3x8_1_e,
       dec3x8_1_f, dec3x8_1_g, dec3x8_1_h, not_1_out, sub_4_1_overflow;
  wire [3:0] add_4_1_s, buffer_6_s, not_4_1_s, or_4_1_s, rot_dir_1_abcd_2, rot_esq_1_abcd_2, sub_4_1_s;

  or or_1 (Overflow, and_2_out, and_1_out);
  and and_1 (and_1_out, sub_4_1_overflow, dec3x8_1_c);
  Dec3x8 dec3x8_1 (
    .a(dec3x8_1_a), .b(dec3x8_1_b), .c(dec3x8_1_c), .d(dec3x8_1_d), .e(dec3x8_1_e), .f(dec3x8_1_f),
    .g(dec3x8_1_g), .h(dec3x8_1_h), .\Operação (in_4));
  and and_2 (and_2_out, add_4_1_overflow, dec3x8_1_b);
  Buffer buffer_1 (.C(dec3x8_1_a), .S(S), .B(B));
  add_4 add_4_1 (.S(add_4_1_s), .Overflow(add_4_1_overflow), .A(A), .B(B));
  Buffer buffer_2 (.C(dec3x8_1_b), .S(S), .B(add_4_1_s));
  sub_4 sub_4_1 (.S(sub_4_1_s), .A(A), .Overflow(sub_4_1_overflow), .B(B));
  Buffer buffer_3 (.C(dec3x8_1_c), .S(S), .B(sub_4_1_s));
  and and_3 (Zero, ~S[0], ~S[1], ~S[2], ~S[3], ~dec3x8_1_g, ~dec3x8_1_h);  // AND_Gate
  OR_4 or_4_1 (.B(B), .A(A), .S(or_4_1_s));
  Buffer buffer_4 (.C(dec3x8_1_d), .S(S), .B(or_4_1_s));
  Not_4 not_4_1 (.B(B), .S(not_4_1_s));
  Buffer buffer_5 (.C(dec3x8_1_e), .S(S), .B(not_4_1_s));
  rot_esq rot_esq_1 (.ABCD_2(rot_esq_1_abcd_2), .abcd(A), .xy(B[1:0]));
  rot_dir rot_dir_1 (.abcd(A), .xy(B[1:0]), .ABCD_2(rot_dir_1_abcd_2));
  not not_1 (not_1_out, D);
  Buffer buffer_6 (.C(not_1_out), .S(buffer_6_s), .B(rot_esq_1_abcd_2));
  Buffer buffer_7 (.C(D), .S(buffer_6_s), .B(rot_dir_1_abcd_2));
  Buffer buffer_8 (.C(dec3x8_1_f), .S(S), .B(buffer_6_s));
endmodule

module Add_1 (
  input  A,
  input  B,
  input  Vem_1,
  output S,
  output Vai_1
);

  wire and_1_out, and_2_out, and_3_out, and_4_out, and_5_out, and_6_out, and_7_out, not_1_out, not_2_out,
       not_3_out, not_4_out, not_5_out, not_6_out;

  not not_1 (not_1_out, A);
  not not_2 (not_2_out, B);
  not not_3 (not_3_out, A);
  not not_4 (not_4_out, Vem_1);
  not not_5 (not_5_out, B);
  not not_6 (not_6_out, Vem_1);
  and and_1 (and_1_out, B, Vem_1);
  and and_2 (and_2_out, A, Vem_1);
  and and_3 (and_3_out, A, B);
  and and_4 (and_4_out, not_1_out, not_2_out, Vem_1);
  and and_5 (and_5_out, not_3_out, B, not_4_out);
  and and_6 (and_6_out, A, not_5_out, not_6_out);
  and and_7 (and_7_out, A, B, Vem_1);
  or or_1 (Vai_1, and_1_out, and_2_out, and_3_out);
  or or_2 (S, and_4_out, and_5_out, and_6_out, and_7_out);
endmodule

module add_4 (
  input  [3:0] A,
  input  [3:0] B,
  output Overflow,
  output [3:0] S
);

  wire add_1_2_vai_1, add_1_3_vai_1, add_1_4_vai_1;

  // Probe on A
  Add_1 add_1_1 (.A(A[3]), .B(B[3]), .Vem_1(add_1_2_vai_1), .S(S[3]), .Vai_1(Overflow));
  Add_1 add_1_2 (.A(A[2]), .B(B[2]), .Vem_1(add_1_3_vai_1), .S(S[2]), .Vai_1(add_1_2_vai_1));
  Add_1 add_1_3 (.A(A[1]), .B(B[1]), .Vem_1(add_1_4_vai_1), .S(S[1]), .Vai_1(add_1_3_vai_1));
  // Probe on S
  Add_1 add_1_4 (.A(A[0]), .B(B[0]), .Vem_1(1'b0), .S(S[0]), .Vai_1(add_1_4_vai_1));
  // Probe on B
endmodule

module OR_4 (
  input  [3:0] B,
  input  [3:0] A,
  output [3:0] S
);

  or or_1 (S[3], A[3], B[3]);
  or or_2 (S[2], A[2], B[2]);
  or or_3 (S[1], A[1], B[1]);
  or or_4 (S[0], A[0], B[0]);
endmodule

module Not_4 (
  input  [3:0] B,
  output [3:0] S
);

  not not_1 (S[3], B[3]);
  not not_2 (S[1], B[1]);
  not not_3 (S[2], B[2]);
  not not_4 (S[0], B[0]);
endmodule

module Buffer (
  input  [3:0] B,
  input  C,
  output [3:0] S
);

  assign S[2] = C ? B[2] : 1'bz;  // Controlled_Buffer controlled_buffer_1
  assign S[3] = C ? B[3] : 1'bz;  // Controlled_Buffer controlled_buffer_2
  assign S[1] = C ? B[1] : 1'bz;  // Controlled_Buffer controlled_buffer_3
  assign S[0] = C ? B[0] : 1'bz;  // Controlled_Buffer controlled_buffer_4
endmodule

module Dec3x8 (
  input  [2:0] \Operação ,
  output a,
  output b,
  output c,
  output d,
  output e,
  output f,
  output g,
  output h
);

  wire not_1_out, not_2_out, not_3_out, not_4_out, not_5_out, not_6_out, not_7_out, not_8_out, not_9_out,
       not_10_out, not_11_out, not_12_out;

  not not_1 (not_1_out, \Operação [2]);
  not not_2 (not_2_out, \Operação [1]);
  not not_3 (not_3_out, \Operação [0]);
  not not_4 (not_4_out, \Operação [2]);
  not not_5 (not_5_out, \Operação [1]);
  not not_6 (not_6_out, \Operação [2]);
  not not_7 (not_7_out, \Operação [0]);
  not not_8 (not_8_out, \Operação [2]);
  not not_9 (not_9_out, \Operação [1]);
  not not_10 (not_10_out, \Operação [0]);
  not not_11 (not_11_out, \Operação [1]);
  not not_12 (not_12_out, \Operação [0]);
  and and_1 (h, \Operação [2], \Operação [1], \Operação [0]);
  and and_2 (a, not_1_out, not_2_out, not_3_out);
  and and_3 (b, not_4_out, not_5_out, \Operação [0]);
  and and_4 (c, not_6_out, \Operação [1], not_7_out);
  and and_5 (d, not_8_out, \Operação [1], \Operação [0]);
  and and_6 (e, \Operação [2], not_9_out, not_10_out);
  and and_7 (f, \Operação [2], not_11_out, \Operação [0]);
  and and_8 (g, \Operação [2], \Operação [1], not_12_out);
endmodule

module rot_esq (
  input  [3:0] abcd,
  input  [1:0] xy,
  output [3:0] ABCD_2
);

  wire and_1_out, and_2_out, and_3_out, and_4_out, and_5_out, and_6_out, and_7_out, and_8_out, and_9_out;

  and and_1 (and_1_out, ~xy[1], ~xy[0], abcd[3]);  // AND_Gate
  and and_2 (and_2_out, ~xy[1], xy[0], abcd[2]);  // AND_Gate
  and and_3 (and_3_out, xy[1], ~xy[0], abcd[1]);  // AND_Gate
  and and_4 (and_4_out, xy[1], xy[0], abcd[0]);
  and and_5 (and_5_out, ~xy[1], ~xy[0], abcd[2]);  // AND_Gate
  and and_6 (and_6_out, ~xy[1], xy[0], abcd[1]);  // AND_Gate
  and and_7 (and_7_out, xy[1], ~xy[0], abcd[0]);  // AND_Gate
  and and_8 (and_8_out, ~xy[1], ~xy[0], abcd[1]);  // AND_Gate
  and and_9 (and_9_out, ~xy[1], xy[0], abcd[0]);  // AND_Gate
  and and_10 (ABCD_2[0], ~xy[1], ~xy[0], abcd[0]);  // AND_Gate
  or or_1 (ABCD_2[1], and_8_out, and_9_out);
  or or_2 (ABCD_2[3], and_1_out, and_2_out, and_3_out, and_4_out);
  or or_3 (ABCD_2[2], and_5_out, and_6_out, and_7_out);
endmodule

module rot_dir (
  input  [3:0] abcd,
  input  [1:0] xy,
  output [3:0] ABCD_2
);

  wire and_2_out, and_3_out, and_4_out, and_5_out, and_6_out, and_7_out, and_8_out, and_9_out, and_10_out;

  and and_1 (ABCD_2[3], ~xy[1], ~xy[0], abcd[3]);  // AND_Gate
  and and_2 (and_2_out, ~xy[1], ~xy[0], abcd[2]);  // AND_Gate
  and and_3 (and_3_out, ~xy[1], xy[0], abcd[3]);  // AND_Gate
  and and_4 (and_4_out, ~xy[1], ~xy[0], abcd[1]);  // AND_Gate
  and and_5 (and_5_out, ~xy[1], xy[0], abcd[2]);  // AND_Gate
  and and_6 (and_6_out, xy[1], ~xy[0], abcd[3]);  // AND_Gate
  and and_7 (and_7_out, ~xy[1], ~xy[0], abcd[0]);  // AND_Gate
  and and_8 (and_8_out, ~xy[1], xy[0], abcd[1]);  // AND_Gate
  and and_9 (and_9_out, xy[1], ~xy[0], abcd[2]);  // AND_Gate
  and and_10 (and_10_out, xy[1], xy[0], abcd[3]);
  or or_1 (ABCD_2[2], and_2_out, and_3_out);
  or or_2 (ABCD_2[1], and_4_out, and_5_out, and_6_out);
  or or_3 (ABCD_2[0], and_7_out, and_8_out, and_9_out, and_10_out);
endmodule

module sub_1 (
  input  A,
  input  B,
  input  VEM1,
  output S,
  output VAI1
);

  wire and_1_out, and_2_out, and_3_out, and_4_out, and_5_out, and_6_out, and_7_out, not_1_out, not_2_out,
       not_3_out, not_4_out, not_5_out, not_6_out, not_7_out, not_8_out;

  not not_1 (not_1_out, A);
  not not_2 (not_2_out, B);
  not not_3 (not_3_out, A);
  not not_4 (not_4_out, VEM1);
  not not_5 (not_5_out, B);
  not not_6 (not_6_out, VEM1);
  not not_7 (not_7_out, A);
  not not_8 (not_8_out, A);
  and and_1 (and_1_out, not_1_out, not_2_out, VEM1);
  and and_2 (and_2_out, not_3_out, B, not_4_out);
  and and_3 (and_3_out, A, not_5_out, not_6_out);
  and and_4 (and_4_out, A, B, VEM1);
  and and_5 (and_5_out, not_7_out, VEM1);
  and and_6 (and_6_out, not_8_out, B);
  and and_7 (and_7_out, B, VEM1);
  or or_1 (S, and_1_out, and_2_out, and_3_out, and_4_out);
  or or_2 (VAI1, and_5_out, and_6_out, and_7_out);
endmodule

module sub_4 (
  input  [3:0] A,
  input  [3:0] B,
  output Overflow,
  output [3:0] S
);

  wire sub_1_2_vai1, sub_1_3_vai1, sub_1_4_vai1;

  // Probe on A
  sub_1 sub_1_1 (.A(A[3]), .B(B[3]), .VEM1(sub_1_3_vai1), .S(S[3]), .VAI1(Overflow));
  sub_1 sub_1_2 (.A(A[1]), .B(B[1]), .VEM1(sub_1_4_vai1), .S(S[1]), .VAI1(sub_1_2_vai1));
  sub_1 sub_1_3 (.A(A[2]), .B(B[2]), .VEM1(sub_1_2_vai1), .S(S[2]), .VAI1(sub_1_3_vai1));
  // Probe on S
  sub_1 sub_1_4 (.A(A[0]), .B(B[0]), .VEM1(1'b0), .S(S[0]), .VAI1(sub_1_4_vai1));
  // Probe on B
endmodule

module AC (
  input  Clock,
  input  [3:0] E,
  output [3:0] out_3
);

  D_Flip_Flop d_ff_1 (.clk(Clock), .D(E[3]), .Q(out_3[3]));  // open: Qn, preset, en, reset
  D_Flip_Flop d_ff_2 (.clk(Clock), .D(E[2]), .Q(out_3[2]));  // open: Qn, preset, en, reset
  D_Flip_Flop d_ff_3 (.clk(Clock), .D(E[1]), .Q(out_3[1]));  // open: Qn, preset, en, reset
  D_Flip_Flop d_ff_4 (.clk(Clock), .D(E[0]), .Q(out_3[0]));  // open: Qn, preset, en, reset
endmodule

module MUX (
  input  [3:0] A,
  input  [3:0] B,
  input  C,
  output [3:0] out_4
);

  wire not_1_out;

  not not_1 (not_1_out, C);
  Buffer buffer_1 (.C(not_1_out), .S(out_4), .B(A));
  Buffer buffer_2 (.C(C), .S(out_4), .B(B));
endmodule

module IR (
  input  Clock,
  input  [7:0] E,
  output [7:0] Q
);

  D_Flip_Flop #(.trigger("falling")) D7 (.clk(Clock), .D(E[7]), .Q(Q[7]));  // open: Qn, preset, en, reset
  D_Flip_Flop #(.trigger("falling")) D6 (.clk(Clock), .D(E[6]), .Q(Q[6]));  // open: Qn, preset, en, reset
  D_Flip_Flop #(.trigger("falling")) D5 (.clk(Clock), .D(E[5]), .Q(Q[5]));  // open: Qn, preset, en, reset
  D_Flip_Flop #(.trigger("falling")) D44 (.clk(Clock), .D(E[4]), .Q(Q[4]));  // open: Qn, preset, en, reset
  D_Flip_Flop #(.trigger("falling")) D3 (.clk(Clock), .D(E[3]), .Q(Q[3]));  // open: Qn, preset, en, reset
  D_Flip_Flop #(.trigger("falling")) D2 (.clk(Clock), .D(E[2]), .Q(Q[2]));  // open: Qn, preset, en, reset
  D_Flip_Flop #(.trigger("falling")) D1 (.clk(Clock), .D(E[1]), .Q(Q[1]));  // open: Qn, preset, en, reset
  D_Flip_Flop #(.trigger("falling")) D0 (.clk(Clock), .D(E[0]), .Q(Q[0]));  // open: Qn, preset, en, reset
endmodule

module UC (
  input  [7:0] \iNSTRUÇÃO ,
  input  Clock,
  input  Reset,
  input  zero,
  input  Overflow,
  output CLK_IR,
  output CLK_AC,
  output [3:0] Dados,
  output CLK_RAM,
  output [3:0] OPERANDO,
  output E,
  output Reset_pc,
  output CLK_PC,
  output [2:0] OPCODE,
  output R_W___0,
  output LOAD
);

  wire GOTO_out, JO_out, JZ_out;
  wire [1:0] counter_1_q;

  Counter #(.width(2), .max('h3)) counter_1 (.Q(counter_1_q), .clk(Clock), .clr(Reset));  // open: load, D, count, carry
  and and_1 (CLK_IR, ~counter_1_q[1], ~counter_1_q[0]);  // AND_Gate
  and and_2 (CLK_PC, ~counter_1_q[1], counter_1_q[0]);  // AND_Gate
  and and_3 (CLK_AC, counter_1_q[1], ~counter_1_q[0]);  // AND_Gate
  and and_4 (CLK_RAM, counter_1_q[1], counter_1_q[0]);
  and JO (JO_out, Overflow, CLK_PC, \iNSTRUÇÃO [7], \iNSTRUÇÃO [6], ~\iNSTRUÇÃO [5], \iNSTRUÇÃO [4]);  // AND_Gate
  and GOTO (GOTO_out, CLK_PC, \iNSTRUÇÃO [7], \iNSTRUÇÃO [6], \iNSTRUÇÃO [5], ~\iNSTRUÇÃO [4]);  // AND_Gate
  and JZ (JZ_out, zero, CLK_PC, \iNSTRUÇÃO [7], \iNSTRUÇÃO [6], ~\iNSTRUÇÃO [5], ~\iNSTRUÇÃO [4]);  // AND_Gate
  nand RW (R_W___0, CLK_AC, \iNSTRUÇÃO [7], \iNSTRUÇÃO [6], \iNSTRUÇÃO [5], \iNSTRUÇÃO [4]);
  or or_1 (LOAD, GOTO_out, JZ_out, JO_out);

  assign Dados = \iNSTRUÇÃO [3:0];
  assign E = \iNSTRUÇÃO [4];
  assign OPCODE = \iNSTRUÇÃO [7:5];
  assign OPERANDO = \iNSTRUÇÃO [3:0];
  assign Reset_pc = Reset;
endmodule
